// Logisim project Project220old.circ as structural Verilog: 1 circuit, main circuit main
module main (
  input  [7:0] X,
  input  [7:0] Y,
  input  [3:0] S3S2S1S0,
  output N,
  output V,
  output [7:0] G,
  output Z,
  output C
);

  wire and_1_out, and_2_out, and_3_out;
  wire [6:0] adder_1_out;
  wire [7:0] multiplexer_1_out, multiplexer_2_out, multiplexer_3_out, multiplexer_4_out, nand_1_out,
       not_1_out, not_2_out, or_1_out, xor_1_out;

  assign not_1_out = ~Y;  // NOT_Gate not_1, 8 bits wide
  assign not_2_out = ~X;  // NOT_Gate not_2, 8 bits wide
  Multiplexer #(.select(2), .width(8)) multiplexer_1 (
    .in0(not_1_out), .in1({8{1'b0}}), .in2(8'h2), .in3(X), .out(multiplexer_1_out), .sel(S3S2S1S0[2:1]));  // open: en
  assign xor_1_out = X ^ Y;  // XOR_Gate xor_1, 8 bits wide
  assign or_1_out = X | not_1_out;  // OR_Gate or_1, 8 bits wide
  assign nand_1_out = ~(X & Y);  // NAND_Gate nand_1, 8 bits wide
  Adder adder_1 (.a(X), .b(multiplexer_1_out), .out({N, adder_1_out}), .cin(S3S2S1S0[0]), .cout(C));
  Multiplexer #(.select(2), .width(8)) multiplexer_2 (
    .in0(xor_1_out), .in1(or_1_out), .in2(nand_1_out), .in3(not_2_out), .out(multiplexer_2_out),
    .sel(S3S2S1S0[1:0]));  // open: en
  Multiplexer #(.width(8)) multiplexer_3 (.out(multiplexer_3_out));  // open: in0, in1, sel, en
  Multiplexer #(.width(8)) multiplexer_4 (
    .in0({N, adder_1_out}), .in1(multiplexer_2_out), .out(multiplexer_4_out), .sel(S3S2S1S0[3]));  // open: en
  Multiplexer #(.width(8)) multiplexer_5 (
    .in0(multiplexer_4_out), .in1(multiplexer_3_out), .out(G), .sel(and_1_out));  // open: en
  and and_1 (and_1_out, S3S2S1S0[3], S3S2S1S0[2]);
  and and_2 (and_2_out, N, ~X[7], ~multiplexer_1_out[7]);  // AND_Gate
  and and_3 (and_3_out, ~N, X[7], multiplexer_1_out[7]);  // AND_Gate
  or or_2 (V, and_2_out, and_3_out);
  nor nor_1 (Z, G[0], G[1], G[2], G[3], G[4], G[5], G[6], G[7]);

  // Notes on the sheet:
  //   arithmetic unit
  //   Logic unit
  //   shifter
  //   ALU
endmodule
